# Fritzing sketch gasture_4WD_robot_fire_fighter (saved by Fritzing 0.9.3b)

parts:
  S1 = H-Bridge with L298N
  U1 = LM2596 step down module
  M3 = Getriebemotor
  M4 = Getriebemotor
  Part2 = Arduino Uno (Rev3)
  HC-SR04_Sensor_1 = HC-SR04 Ultrasonic Distance Sensor
  Flame_Sensor_Module1 = Flame Sensor Module [part_number="Flame Sensor Module" chip_label=IC package="DIP (Dual Inline) [THT]"]
  Part3 = Jtron 1 Channel Optoisolated Relay Module [package=relay]
  M5 = DC Motor
  J1 = Basic Servo
  A1 = NRF24L01-BO-with-pcb [package=THT]
  C1 = Ceramic Capacitor [capacitance=100nF package="100 mil [THT, multilayer]"]
  M6 = Getriebemotor
  M7 = Getriebemotor
  VCC1 = 4 x AAA Battery Mount
  U2 = SWITCH-SPST-2 [package=r_sw_th]

nets:
  N1: S1.12V, U1.OUT+, Part3.MAIN
  GND: S1.GND, U1.IN-, U1.OUT-, Part2.GND, HC-SR04_Sensor_1.GND, Flame_Sensor_Module1.GND, Part3.GND, M5.pin_1, J1.gnd, A1.GND, C1.1, VCC1.-
  VCC: S1.5V, Part2.5V, HC-SR04_Sensor_1.VCC, Flame_Sensor_Module1.VCC, Part3.VCC, J1.vcc, A1.VCC
  N2: S1.ENA, Part2.D5_PWM
  N3: S1.IN1, Part2.D2
  N4: S1.IN2, Part2.D3_PWM
  N5: S1.IN3, Part2.D4
  N6: S1.IN4, Part2.D7
  N7: S1.ENB, Part2.D6_PWM
  N8: S1.M1-01, M7.pin_2
  N9: S1.M1-02, M3.pin_1, M7.pin_1
  N10: S1.M2-01, M4.pin_2, M6.pin_2
  N11: S1.M2-02, M4.pin_1, M6.pin_1
  N12: U1.IN+, U2.P
  N13: Part2.A1, Part3.IN1
  N14: Part2.A2, J1.pulse
  N15: Part2.A3, Flame_Sensor_Module1.DO
  N16: Part2.A4/SDA, HC-SR04_Sensor_1.TRIG
  N17: Part2.A5/SCL, HC-SR04_Sensor_1.ECHO
  N18: Part2.D8, A1.CE
  N19: Part2.D9_PWM, A1.CSN
  N20: Part2.D11_PWM/MOSI, A1.M0
  N21: Part2.D12/MISO, A1.M1
  N22: Part2.D13/SCK, A1.SCK
  N23: Part3.NO, M5.pin_2, C1.0
  N24: VCC1.+, U2.O

custom parts:
  H-Bridge with L298N: h-bridge
  LM2596 step down module: LM2596 DC-DC step down power supply module 3 A.
  HC-SR04 Ultrasonic Distance Sensor: The HC-SR04 is an ultrasonic distance sensor. It is capable of providing measurement for ranges of 2cm to 400cm. The module operates at 5V.
  Flame Sensor Module: A simple fire/flame sensor where you can easily detect fire interfacing with gizduino boards mcu. By reading the Digital output of the sensor, 0 - if there's a on fire, 1 - no fire detected. With 1 meter range detection (max sensitive adjustment. sensor.
  NRF24L01-BO-with-pcb: NRF24L01-BO breakout board for the NRF24L01. Pcb view included.
