# Fritzing sketch gasture_4WD_robot_fire_fighter_t (saved by Fritzing 0.9.3b)
breadboards: 1

parts:
  Part1 = Arduino Nano (Rev3.0)
  A1 = NRF24L01-BO-with-pcb [package=THT]
  GY1 = MPU-6050 Board GY-521 [form="♀ (female)" package=THT]
  VCC1 = 4 x AAA Battery Mount

nets:
  GND: Part1.GND, A1.GND, GY1.pin2, VCC1.-
  N1: Part1.D7, A1.CE
  N2: Part1.D8, A1.CSN
  N3: Part1.D11/MOSI, A1.M0
  N4: Part1.D12/MISO, A1.M1
  N5: Part1.VIN, VCC1.+
  5V: Part1.5V, A1.VCC, GY1.pin1
  N6: Part1.A5, GY1.pin3
  N7: Part1.A4, GY1.pin4
  N8: Part1.D13/SCK, A1.SCK

custom parts:
  NRF24L01-BO-with-pcb: NRF24L01-BO breakout board for the NRF24L01. Pcb view included.
  MPU-6050 Board GY-521: Acelerometro y Giroscopio MPU-6050 Board GY-521
